// Logisim project 2ADD.circ as structural Verilog: 1 circuit, main circuit main
module main (
  input  in_1,
  input  in_2,
  input  in_3,
  input  in_4,
  input  in_5
);

  wire transistor_1_out, transistor_3_out, transistor_5_out, transistor_7_out, transistor_9_out,
       transistor_10_out, transistor_11_out, transistor_12_out, transistor_13_out, transistor_14_out,
       transistor_17_out, transistor_20_out, transistor_23_out, transistor_26_out, transistor_29_out,
       transistor_32_out, transistor_33_out, transistor_35_out, transistor_37_out, transistor_39_out,
       transistor_41_out, transistor_43_out, transistor_45_out, transistor_46_out, transistor_49_out,
       transistor_50_out, transistor_51_out, transistor_52_out, transistor_53_out, transistor_54_out,
       transistor_56_out, transistor_57_out, transistor_61_out, transistor_63_out, transistor_64_out,
       transistor_66_out, transistor_67_out, transistor_71_out, transistor_75_out, transistor_78_out,
       transistor_79_out, transistor_83_out, transistor_86_out, transistor_87_out, transistor_89_out,
       transistor_91_out, transistor_93_out, transistor_95_out, transistor_97_out, transistor_99_out;

  Transistor transistor_1 (.in(1'b1), .out(transistor_1_out), .gate(in_2));
  Transistor #(.\type ("n")) transistor_2 (.in(1'b0), .out(transistor_1_out), .gate(in_2));
  Transistor transistor_3 (.in(1'b1), .out(transistor_3_out), .gate(in_3));
  Transistor #(.\type ("n")) transistor_4 (.in(1'b0), .out(transistor_3_out), .gate(in_3));
  Transistor transistor_5 (.in(1'b1), .out(transistor_5_out), .gate(in_4));
  Transistor #(.\type ("n")) transistor_6 (.in(1'b0), .out(transistor_5_out), .gate(in_4));
  Transistor transistor_7 (.in(1'b1), .out(transistor_7_out), .gate(in_5));
  Transistor #(.\type ("n")) transistor_8 (.in(1'b0), .out(transistor_7_out), .gate(in_5));
  Transistor transistor_9 (.in(1'b1), .out(transistor_9_out), .gate(transistor_1_out));
  Transistor transistor_10 (.in(1'b1), .out(transistor_10_out), .gate(transistor_3_out));
  Transistor transistor_11 (.in(1'b1), .out(transistor_11_out), .gate(in_2));
  Transistor transistor_12 (.in(1'b1), .out(transistor_12_out), .gate(transistor_5_out));
  Transistor transistor_13 (.in(1'b1), .out(transistor_13_out), .gate(transistor_7_out));
  Transistor transistor_14 (.in(1'b1), .out(transistor_14_out), .gate(in_4));
  Transistor transistor_15 (.in(1'b1), .out(transistor_9_out), .gate(in_3));
  Transistor #(.\type ("n")) transistor_16 (.in(transistor_17_out), .out(transistor_9_out), .gate(transistor_1_out));
  Transistor #(.\type ("n")) transistor_17 (.in(1'b0), .out(transistor_17_out), .gate(in_3));
  Transistor transistor_18 (.in(1'b1), .out(transistor_10_out), .gate(in_2));
  Transistor #(.\type ("n")) transistor_19 (.in(transistor_20_out), .out(transistor_10_out), .gate(transistor_3_out));
  Transistor #(.\type ("n")) transistor_20 (.in(1'b0), .out(transistor_20_out), .gate(in_2));
  Transistor transistor_21 (.in(1'b1), .out(transistor_11_out), .gate(in_3));
  Transistor #(.\type ("n")) transistor_22 (.in(transistor_23_out), .out(transistor_11_out), .gate(in_2));
  Transistor #(.\type ("n")) transistor_23 (.in(1'b0), .out(transistor_23_out), .gate(in_3));
  Transistor transistor_24 (.in(1'b1), .out(transistor_12_out), .gate(in_5));
  Transistor #(.\type ("n")) transistor_25 (.in(transistor_26_out), .out(transistor_12_out), .gate(transistor_5_out));
  Transistor #(.\type ("n")) transistor_26 (.in(1'b0), .out(transistor_26_out), .gate(in_5));
  Transistor transistor_27 (.in(1'b1), .out(transistor_13_out), .gate(in_4));
  Transistor #(.\type ("n")) transistor_28 (.in(transistor_29_out), .out(transistor_13_out), .gate(transistor_7_out));
  Transistor #(.\type ("n")) transistor_29 (.in(1'b0), .out(transistor_29_out), .gate(in_4));
  Transistor transistor_30 (.in(1'b1), .out(transistor_14_out), .gate(in_5));
  Transistor #(.\type ("n")) transistor_31 (.in(transistor_32_out), .out(transistor_14_out), .gate(in_4));
  Transistor #(.\type ("n")) transistor_32 (.in(1'b0), .out(transistor_32_out), .gate(in_5));
  Transistor transistor_33 (.in(1'b1), .out(transistor_33_out), .gate(transistor_9_out));
  Transistor #(.\type ("n")) transistor_34 (.in(1'b0), .out(transistor_33_out), .gate(transistor_9_out));
  Transistor transistor_35 (.in(1'b1), .out(transistor_35_out), .gate(transistor_10_out));
  Transistor #(.\type ("n")) transistor_36 (.in(1'b0), .out(transistor_35_out), .gate(transistor_10_out));
  Transistor transistor_37 (.in(1'b1), .out(transistor_37_out), .gate(transistor_11_out));
  Transistor #(.\type ("n")) transistor_38 (.in(1'b0), .out(transistor_37_out), .gate(transistor_11_out));
  Transistor transistor_39 (.in(1'b1), .out(transistor_39_out), .gate(transistor_12_out));
  Transistor #(.\type ("n")) transistor_40 (.in(1'b0), .out(transistor_39_out), .gate(transistor_12_out));
  Transistor transistor_41 (.in(1'b1), .out(transistor_41_out), .gate(transistor_13_out));
  Transistor #(.\type ("n")) transistor_42 (.in(1'b0), .out(transistor_41_out), .gate(transistor_13_out));
  Transistor transistor_43 (.in(1'b1), .out(transistor_43_out), .gate(transistor_14_out));
  Transistor #(.\type ("n")) transistor_44 (.in(1'b0), .out(transistor_43_out), .gate(transistor_14_out));
  Transistor #(.\type ("n")) transistor_45 (.in(1'b1), .out(transistor_45_out), .gate(transistor_35_out));
  Transistor #(.\type ("n")) transistor_46 (.in(1'b1), .out(transistor_46_out), .gate(transistor_41_out));
  Transistor #(.\type ("n")) transistor_47 (.in(1'b1), .out(transistor_45_out), .gate(transistor_33_out));
  Pull_Resistor pull_resistor_1 (.node(transistor_45_out));
  Transistor #(.\type ("n")) transistor_48 (.in(1'b1), .out(transistor_46_out), .gate(transistor_39_out));
  Pull_Resistor pull_resistor_2 (.node(transistor_46_out));
  Transistor transistor_49 (.in(1'b1), .out(transistor_49_out), .gate(transistor_45_out));
  Transistor #(.\type ("n")) transistor_50 (.in(1'b1), .out(transistor_50_out), .gate(transistor_37_out));
  Pull_Resistor pull_resistor_3 (.node(transistor_50_out));
  LED led_1 (.in(transistor_50_out));
  Transistor transistor_51 (.in(1'b1), .out(transistor_51_out), .gate(transistor_46_out));
  Transistor #(.\type ("n")) transistor_52 (.in(1'b1), .out(transistor_52_out), .gate(transistor_43_out));
  Pull_Resistor pull_resistor_4 (.node(transistor_52_out));
  Transistor transistor_53 (.in(1'b1), .out(transistor_53_out), .gate(transistor_54_out));
  Transistor transistor_54 (.in(1'b1), .out(transistor_54_out), .gate(in_1));
  Transistor #(.\type ("n")) transistor_55 (.in(1'b0), .out(transistor_54_out), .gate(in_1));
  Transistor transistor_56 (.in(1'b1), .out(transistor_56_out), .gate(transistor_57_out));
  Transistor transistor_57 (.in(1'b1), .out(transistor_57_out), .gate(transistor_45_out));
  Transistor #(.\type ("n")) transistor_58 (.in(1'b0), .out(transistor_57_out), .gate(transistor_45_out));
  Transistor transistor_59 (.in(1'b1), .out(transistor_49_out), .gate(in_1));
  Transistor #(.\type ("n")) transistor_60 (.in(transistor_61_out), .out(transistor_49_out), .gate(transistor_45_out));
  Transistor #(.\type ("n")) transistor_61 (.in(1'b0), .out(transistor_61_out), .gate(in_1));
  Transistor #(.\type ("n")) transistor_62 (.in(1'b1), .out(transistor_50_out), .gate(transistor_79_out));
  Transistor transistor_63 (.in(1'b1), .out(transistor_63_out), .gate(transistor_64_out));
  Transistor transistor_64 (.in(1'b1), .out(transistor_64_out), .gate(transistor_50_out));
  Transistor #(.\type ("n")) transistor_65 (.in(1'b0), .out(transistor_64_out), .gate(transistor_50_out));
  Transistor transistor_66 (.in(1'b1), .out(transistor_66_out), .gate(transistor_67_out));
  Transistor transistor_67 (.in(1'b1), .out(transistor_67_out), .gate(transistor_46_out));
  Transistor #(.\type ("n")) transistor_68 (.in(1'b0), .out(transistor_67_out), .gate(transistor_46_out));
  Transistor transistor_69 (.in(1'b1), .out(transistor_51_out), .gate(transistor_50_out));
  Transistor #(.\type ("n")) transistor_70 (.in(transistor_71_out), .out(transistor_51_out), .gate(transistor_46_out));
  Transistor #(.\type ("n")) transistor_71 (.in(1'b0), .out(transistor_71_out), .gate(transistor_50_out));
  Transistor #(.\type ("n")) transistor_72 (.in(1'b1), .out(transistor_52_out), .gate(transistor_87_out));
  Transistor transistor_73 (.in(1'b1), .out(transistor_53_out), .gate(transistor_45_out));
  Transistor #(.\type ("n")) transistor_74 (.in(transistor_75_out), .out(transistor_53_out), .gate(transistor_54_out));
  Transistor #(.\type ("n")) transistor_75 (.in(1'b0), .out(transistor_75_out), .gate(transistor_45_out));
  Transistor transistor_76 (.in(1'b1), .out(transistor_56_out), .gate(in_1));
  Transistor #(.\type ("n")) transistor_77 (.in(transistor_78_out), .out(transistor_56_out), .gate(transistor_57_out));
  Transistor #(.\type ("n")) transistor_78 (.in(1'b0), .out(transistor_78_out), .gate(in_1));
  Transistor transistor_79 (.in(1'b1), .out(transistor_79_out), .gate(transistor_49_out));
  Transistor #(.\type ("n")) transistor_80 (.in(1'b0), .out(transistor_79_out), .gate(transistor_49_out));
  Transistor transistor_81 (.in(1'b1), .out(transistor_63_out), .gate(transistor_46_out));
  Transistor #(.\type ("n")) transistor_82 (.in(transistor_83_out), .out(transistor_63_out), .gate(transistor_64_out));
  Transistor #(.\type ("n")) transistor_83 (.in(1'b0), .out(transistor_83_out), .gate(transistor_46_out));
  Transistor transistor_84 (.in(1'b1), .out(transistor_66_out), .gate(transistor_50_out));
  Transistor #(.\type ("n")) transistor_85 (.in(transistor_86_out), .out(transistor_66_out), .gate(transistor_67_out));
  Transistor #(.\type ("n")) transistor_86 (.in(1'b0), .out(transistor_86_out), .gate(transistor_50_out));
  Transistor transistor_87 (.in(1'b1), .out(transistor_87_out), .gate(transistor_51_out));
  Transistor #(.\type ("n")) transistor_88 (.in(1'b0), .out(transistor_87_out), .gate(transistor_51_out));
  Transistor transistor_89 (.in(1'b1), .out(transistor_89_out), .gate(transistor_53_out));
  Transistor #(.\type ("n")) transistor_90 (.in(1'b0), .out(transistor_89_out), .gate(transistor_53_out));
  Transistor transistor_91 (.in(1'b1), .out(transistor_91_out), .gate(transistor_56_out));
  Transistor #(.\type ("n")) transistor_92 (.in(1'b0), .out(transistor_91_out), .gate(transistor_56_out));
  Transistor transistor_93 (.in(1'b1), .out(transistor_93_out), .gate(transistor_63_out));
  Transistor #(.\type ("n")) transistor_94 (.in(1'b0), .out(transistor_93_out), .gate(transistor_63_out));
  Transistor transistor_95 (.in(1'b1), .out(transistor_95_out), .gate(transistor_66_out));
  Transistor #(.\type ("n")) transistor_96 (.in(1'b0), .out(transistor_95_out), .gate(transistor_66_out));
  Transistor #(.\type ("n")) transistor_97 (.in(1'b1), .out(transistor_97_out), .gate(transistor_89_out));
  Pull_Resistor pull_resistor_5 (.node(transistor_97_out));
  Transistor #(.\type ("n")) transistor_98 (.in(1'b1), .out(transistor_97_out), .gate(transistor_91_out));
  Transistor #(.\type ("n")) transistor_99 (.in(1'b1), .out(transistor_99_out), .gate(transistor_93_out));
  Transistor #(.\type ("n")) transistor_100 (.in(1'b1), .out(transistor_99_out), .gate(transistor_95_out));
  Pull_Resistor pull_resistor_6 (.node(transistor_99_out));
  LED led_2 (.in(transistor_97_out));
  LED led_3 (.in(transistor_99_out));
  LED led_4 (.in(transistor_52_out));

  // Notes on the sheet:
  //   5V
  //   NOT
  //   NOT
  //   NOT
  //   NOT
endmodule
