// Logisim project ADD.circ as structural Verilog: 1 circuit, main circuit main
module main (
  input  in_1,
  input  NOT,
  input  in_3
);

  wire transistor_1_out, transistor_3_out, transistor_5_out, transistor_6_out, transistor_7_out,
       transistor_10_out, transistor_13_out, transistor_16_out, transistor_17_out, transistor_19_out,
       transistor_21_out, transistor_23_out, transistor_25_out, transistor_26_out, transistor_27_out,
       transistor_28_out, transistor_30_out, transistor_31_out, transistor_35_out, transistor_39_out,
       transistor_42_out, transistor_43_out, transistor_45_out, transistor_47_out, transistor_49_out;

  Transistor transistor_1 (.in(1'b1), .out(transistor_1_out), .gate(NOT));
  Transistor #(.\type ("n")) transistor_2 (.in(1'b0), .out(transistor_1_out), .gate(NOT));
  Transistor transistor_3 (.in(1'b1), .out(transistor_3_out), .gate(in_3));
  Transistor #(.\type ("n")) transistor_4 (.in(1'b0), .out(transistor_3_out), .gate(in_3));
  Transistor transistor_5 (.in(1'b1), .out(transistor_5_out), .gate(transistor_1_out));
  Transistor transistor_6 (.in(1'b1), .out(transistor_6_out), .gate(transistor_3_out));
  Transistor transistor_7 (.in(1'b1), .out(transistor_7_out), .gate(NOT));
  Transistor transistor_8 (.in(1'b1), .out(transistor_5_out), .gate(in_3));
  Transistor #(.\type ("n")) transistor_9 (.in(transistor_10_out), .out(transistor_5_out), .gate(transistor_1_out));
  Transistor #(.\type ("n")) transistor_10 (.in(1'b0), .out(transistor_10_out), .gate(in_3));
  Transistor transistor_11 (.in(1'b1), .out(transistor_6_out), .gate(NOT));
  Transistor #(.\type ("n")) transistor_12 (.in(transistor_13_out), .out(transistor_6_out), .gate(transistor_3_out));
  Transistor #(.\type ("n")) transistor_13 (.in(1'b0), .out(transistor_13_out), .gate(NOT));
  Transistor transistor_14 (.in(1'b1), .out(transistor_7_out), .gate(in_3));
  Transistor #(.\type ("n")) transistor_15 (.in(transistor_16_out), .out(transistor_7_out), .gate(NOT));
  Transistor #(.\type ("n")) transistor_16 (.in(1'b0), .out(transistor_16_out), .gate(in_3));
  Transistor transistor_17 (.in(1'b1), .out(transistor_17_out), .gate(transistor_5_out));
  Transistor #(.\type ("n")) transistor_18 (.in(1'b0), .out(transistor_17_out), .gate(transistor_5_out));
  Transistor transistor_19 (.in(1'b1), .out(transistor_19_out), .gate(transistor_6_out));
  Transistor #(.\type ("n")) transistor_20 (.in(1'b0), .out(transistor_19_out), .gate(transistor_6_out));
  Transistor transistor_21 (.in(1'b1), .out(transistor_21_out), .gate(transistor_7_out));
  Transistor #(.\type ("n")) transistor_22 (.in(1'b0), .out(transistor_21_out), .gate(transistor_7_out));
  Transistor #(.\type ("n")) transistor_23 (.in(1'b1), .out(transistor_23_out), .gate(transistor_19_out));
  Transistor #(.\type ("n")) transistor_24 (.in(1'b1), .out(transistor_23_out), .gate(transistor_17_out));
  Pull_Resistor pull_resistor_1 (.node(transistor_23_out));
  Transistor transistor_25 (.in(1'b1), .out(transistor_25_out), .gate(transistor_23_out));
  Transistor #(.\type ("n")) transistor_26 (.in(1'b1), .out(transistor_26_out), .gate(transistor_21_out));
  Pull_Resistor pull_resistor_2 (.node(transistor_26_out));
  LED led_1 (.in(transistor_26_out));
  Transistor transistor_27 (.in(1'b1), .out(transistor_27_out), .gate(transistor_28_out));
  Transistor transistor_28 (.in(1'b1), .out(transistor_28_out), .gate(in_1));
  Transistor #(.\type ("n")) transistor_29 (.in(1'b0), .out(transistor_28_out), .gate(in_1));
  Transistor transistor_30 (.in(1'b1), .out(transistor_30_out), .gate(transistor_31_out));
  Transistor transistor_31 (.in(1'b1), .out(transistor_31_out), .gate(transistor_23_out));
  Transistor #(.\type ("n")) transistor_32 (.in(1'b0), .out(transistor_31_out), .gate(transistor_23_out));
  Transistor transistor_33 (.in(1'b1), .out(transistor_25_out), .gate(in_1));
  Transistor #(.\type ("n")) transistor_34 (.in(transistor_35_out), .out(transistor_25_out), .gate(transistor_23_out));
  Transistor #(.\type ("n")) transistor_35 (.in(1'b0), .out(transistor_35_out), .gate(in_1));
  Transistor #(.\type ("n")) transistor_36 (.in(1'b1), .out(transistor_26_out), .gate(transistor_43_out));
  Transistor transistor_37 (.in(1'b1), .out(transistor_27_out), .gate(transistor_23_out));
  Transistor #(.\type ("n")) transistor_38 (.in(transistor_39_out), .out(transistor_27_out), .gate(transistor_28_out));
  Transistor #(.\type ("n")) transistor_39 (.in(1'b0), .out(transistor_39_out), .gate(transistor_23_out));
  Transistor transistor_40 (.in(1'b1), .out(transistor_30_out), .gate(in_1));
  Transistor #(.\type ("n")) transistor_41 (.in(transistor_42_out), .out(transistor_30_out), .gate(transistor_31_out));
  Transistor #(.\type ("n")) transistor_42 (.in(1'b0), .out(transistor_42_out), .gate(in_1));
  Transistor transistor_43 (.in(1'b1), .out(transistor_43_out), .gate(transistor_25_out));
  Transistor #(.\type ("n")) transistor_44 (.in(1'b0), .out(transistor_43_out), .gate(transistor_25_out));
  Transistor transistor_45 (.in(1'b1), .out(transistor_45_out), .gate(transistor_27_out));
  Transistor #(.\type ("n")) transistor_46 (.in(1'b0), .out(transistor_45_out), .gate(transistor_27_out));
  Transistor transistor_47 (.in(1'b1), .out(transistor_47_out), .gate(transistor_30_out));
  Transistor #(.\type ("n")) transistor_48 (.in(1'b0), .out(transistor_47_out), .gate(transistor_30_out));
  Transistor #(.\type ("n")) transistor_49 (.in(1'b1), .out(transistor_49_out), .gate(transistor_45_out));
  Transistor #(.\type ("n")) transistor_50 (.in(1'b1), .out(transistor_49_out), .gate(transistor_47_out));
  Pull_Resistor pull_resistor_3 (.node(transistor_49_out));
  LED led_2 (.in(transistor_49_out));

  // Notes on the sheet:
  //   NOT
  //   AND
  //   NOT
  //   AND
  //   OR
  //   NOT
  //   OR
  //   NOT
  //   NOT
  //   NOT
  //   NOT
endmodule
