// Logisim project BUS.circ as structural Verilog: 1 circuit, main circuit main
module main (
  input  [7:0] in_1,
  input  [7:0] in_2
);

  wire clock_1_out, not_1_out;
  wire [7:0] register_1_q, register_2_q, transistor_1_out, transistor_4_out;

  ROM rom_1 ();  // open: addr, data, sel
  RAM ram_1 ();  // open: addr, data, sel, clk, ld, clr
  Transistor #(.\type ("n"), .width(8)) transistor_1 (.in(in_2), .out(transistor_1_out), .gate(transistor_4_out[0]));
  Transistor #(.\type ("n"), .width(8)) transistor_2 (
    .in(register_1_q), .out(transistor_1_out), .gate(transistor_4_out[1]));
  Transistor #(.\type ("n"), .width(8)) transistor_3 (
    .in(register_2_q), .out(transistor_1_out), .gate(transistor_4_out[2]));
  Clock clock_1 (.out(clock_1_out));
  not not_1 (not_1_out, clock_1_out);
  Register register_1 (
    .D(transistor_1_out), .en(transistor_4_out[3]), .Q(register_1_q), .clk(clock_1_out),
    .clr(transistor_4_out[7]));
  Register register_2 (
    .D(transistor_1_out), .en(transistor_4_out[4]), .Q(register_2_q), .clk(clock_1_out),
    .clr(transistor_4_out[7]));
  Transistor #(.\type ("n"), .width(8)) transistor_4 (.in(in_1), .out(transistor_4_out), .gate(not_1_out));
  Pull_Resistor pull_resistor_1 (.node(transistor_4_out[4]));
  Pull_Resistor pull_resistor_2 (.node(transistor_4_out[2]));
  Pull_Resistor pull_resistor_3 (.node(transistor_4_out[1]));
  Pull_Resistor pull_resistor_4 (.node(transistor_4_out[6]));
  Pull_Resistor pull_resistor_5 (.node(transistor_4_out[3]));
  Pull_Resistor pull_resistor_6 (.node(transistor_4_out[0]));
  Pull_Resistor pull_resistor_7 (.node(transistor_4_out[5]));
  Pull_Resistor pull_resistor_8 (.node(transistor_4_out[7]));
endmodule
