// Logisim project GATES.circ as structural Verilog: 1 circuit, main circuit main
module main (
  input  in_1,
  input  in_2,
  input  in_3,
  input  in_4,
  input  in_5
);

  wire transistor_1_out, transistor_2_out, transistor_3_out, transistor_4_out;

  Transistor transistor_1 (.in(1'b1), .out(transistor_1_out), .gate(in_1));
  Pull_Resistor pull_resistor_1 (.node(transistor_1_out));
  LED led_1 (.in(transistor_1_out));
  Transistor #(.\type ("n")) transistor_2 (.in(1'b1), .out(transistor_2_out), .gate(in_2));
  Transistor #(.\type ("n")) transistor_3 (.in(transistor_2_out), .out(transistor_3_out), .gate(in_4));
  LED led_2 (.in(transistor_3_out));
  Pull_Resistor pull_resistor_2 (.node(transistor_3_out));
  Transistor #(.\type ("n")) transistor_4 (.in(1'b1), .out(transistor_4_out), .gate(in_3));
  Pull_Resistor pull_resistor_3 (.node(transistor_4_out));
  Transistor #(.\type ("n")) transistor_5 (.in(1'b1), .out(transistor_4_out), .gate(in_5));
  LED led_3 (.in(transistor_4_out));
endmodule
