// Logisim project IC.circ as structural Verilog
module main (
);

  wire clock_1_out, E0, E1, E2, E3, E4, E5, E6, E7, n00ls245_1_a1, n00ls245_1_a2, n00ls245_1_a3,
       n00ls245_1_a4, n00ls245_1_a5, n00ls245_1_a6, n00ls245_1_a7, n00ls245_1_a8, n74ls04_1_y6,
       n74ls161n_1_qa, n74ls161n_1_qb, n74ls161n_1_qc, n74ls161n_1_qd, n74ls173_3_q1, n74ls173_3_q2,
       n74ls173_3_q3, n74ls173_3_q4, n74ls173_4_q1, n74ls173_4_q2, n74ls173_4_q3, n74ls173_4_q4,
       n74ls283_1_c4, R0, R1, R2, R3, R4, R5, R6, R7;
  wire [7:0] n28c16_1_dq0, pull_resistor_9_node;

  _74LS283 u_74ls283_1 (
    .VCC(1'b1), .A3(R2), .E3(E2), .A4(R3), .E4(E3), .C4(n74ls283_1_c4), .E2(E1), .A2(R1), .E1(E0), .A1(R0),
    .B1(1'b1), .GND(1'b0));  // open: B3, B4, B2, C0
  _74LS283 u_74ls283_2 (
    .VCC(1'b1), .A3(R6), .E3(E6), .A4(R7), .E4(E7), .E2(E5), .A2(R5), .E1(E4), .A1(R4), .C0(n74ls283_1_c4),
    .GND(1'b0));  // open: B3, B4, C4, B2, B1
  LED led_1 (.in(n00ls245_1_a7));
  LED led_2 (.in(n00ls245_1_a8));
  LED led_3 (.in(n00ls245_1_a6));
  LED led_4 (.in(n00ls245_1_a5));
  _00LS245 u_00ls245_1 (
    .VCC(pull_resistor_9_node[2]), .G(pull_resistor_9_node[2]), .B1(E0), .B2(E1), .B3(E2), .B4(E3), .B5(E4),
    .B6(E5), .B7(E6), .B8(E7), .A1(n00ls245_1_a1), .A2(n00ls245_1_a2), .A3(n00ls245_1_a3),
    .A4(n00ls245_1_a4), .A5(n00ls245_1_a5), .A6(n00ls245_1_a6), .A7(n00ls245_1_a7), .A8(n00ls245_1_a8));  // open: DIR, GND
  LED led_5 (.in(n00ls245_1_a2));
  LED led_6 (.in(n00ls245_1_a3));
  LED led_7 (.in(n00ls245_1_a4));
  LED LSB (.in(n00ls245_1_a1));
  _74LS173 u_74ls173_1 (
    .VCC(pull_resistor_9_node[0]), .D1(n00ls245_1_a5), .D2(n00ls245_1_a6), .D3(n00ls245_1_a7),
    .D4(n00ls245_1_a8), .G2(pull_resistor_9_node[0]), .G1(pull_resistor_9_node[0]), .M(1'b1), .N(1'b1),
    .Q1(R4), .Q2(R5), .Q3(R6), .Q4(R7), .CLK(clock_1_out), .GND(1'b0));  // open: CLR
  _74LS173 u_74ls173_2 (
    .VCC(pull_resistor_9_node[0]), .D1(n00ls245_1_a1), .D2(n00ls245_1_a2), .D3(n00ls245_1_a3),
    .D4(n00ls245_1_a4), .G2(pull_resistor_9_node[0]), .G1(pull_resistor_9_node[0]), .M(1'b1), .N(1'b1),
    .Q1(R0), .Q2(R1), .Q3(R2), .Q4(R3), .CLK(clock_1_out), .GND(1'b0));  // open: CLR
  _00LS245 u_00ls245_2 (
    .VCC(pull_resistor_9_node[1]), .G(pull_resistor_9_node[1]), .B1(R0), .B2(R1), .B3(R2), .B4(R3), .B5(R4),
    .B6(R5), .B7(R6), .B8(R7), .A1(n00ls245_1_a1), .A2(n00ls245_1_a2), .A3(n00ls245_1_a3),
    .A4(n00ls245_1_a4), .A5(n00ls245_1_a5), .A6(n00ls245_1_a6), .A7(n00ls245_1_a7), .A8(n00ls245_1_a8),
    .GND(1'b0));  // open: DIR
  _74LS173 u_74ls173_3 (
    .VCC(pull_resistor_9_node[3]), .D1(n00ls245_1_a5), .D2(n00ls245_1_a6), .D3(n00ls245_1_a7),
    .D4(n00ls245_1_a8), .G2(pull_resistor_9_node[3]), .G1(pull_resistor_9_node[3]), .M(1'b1), .N(1'b1),
    .Q1(n74ls173_3_q1), .Q2(n74ls173_3_q2), .Q3(n74ls173_3_q3), .Q4(n74ls173_3_q4), .CLK(clock_1_out),
    .GND(1'b0));  // open: CLR
  _74LS173 u_74ls173_4 (
    .VCC(pull_resistor_9_node[3]), .D1(n00ls245_1_a1), .D2(n00ls245_1_a2), .D3(n00ls245_1_a3),
    .D4(n00ls245_1_a4), .G2(pull_resistor_9_node[3]), .G1(pull_resistor_9_node[3]), .M(1'b1), .N(1'b1),
    .Q1(n74ls173_4_q1), .Q2(n74ls173_4_q2), .Q3(n74ls173_4_q3), .Q4(n74ls173_4_q4), .CLK(clock_1_out),
    .GND(1'b0));  // open: CLR
  _00LS245 u_00ls245_3 (
    .VCC(pull_resistor_9_node[4]), .G(pull_resistor_9_node[4]), .B1(n74ls173_4_q1), .B2(n74ls173_4_q2),
    .B3(n74ls173_4_q3), .B4(n74ls173_4_q4), .B5(n74ls173_3_q1), .B6(n74ls173_3_q2), .B7(n74ls173_3_q3),
    .B8(n74ls173_3_q4), .A1(n00ls245_1_a1), .A2(n00ls245_1_a2), .A3(n00ls245_1_a3), .A4(n00ls245_1_a4),
    .A5(n00ls245_1_a5), .A6(n00ls245_1_a6), .A7(n00ls245_1_a7), .A8(n00ls245_1_a8), .GND(1'b0));  // open: DIR
  Hex_Digit_Display hex_digit_display_1 (.value({R3, R2, R1, R0}));  // open: dp
  Hex_Digit_Display hex_digit_display_2 (.value({R7, R6, R5, R4}));  // open: dp
  Clock clock_1 (.out(clock_1_out));
  Pull_Resistor pull_resistor_1 (.node(clock_1_out));
  Pull_Resistor pull_resistor_2 (.node(pull_resistor_9_node[4]));
  Pull_Resistor pull_resistor_3 (.node(pull_resistor_9_node[2]));
  Pull_Resistor pull_resistor_4 (.node(pull_resistor_9_node[6]));
  Pull_Resistor pull_resistor_5 (.node(pull_resistor_9_node[5]));
  Pull_Resistor pull_resistor_6 (.node(pull_resistor_9_node[3]));
  Pull_Resistor pull_resistor_7 (.node(pull_resistor_9_node[7]));
  Pull_Resistor pull_resistor_8 (.node(pull_resistor_9_node[1]));
  Pull_Resistor pull_resistor_9 (.node(pull_resistor_9_node[0]));
  _74LS04 u_74ls04_1 (
    .VCC(1'b1), .A6(clock_1_out), .Y6(n74ls04_1_y6), .GND(1'b0));  // open: A5, Y5, A4, Y4, A1, Y1, A2, Y2, A3, Y3
  LED led_8 (.in(n74ls161n_1_qc));
  LED led_9 (.in(n74ls161n_1_qb));
  LED led_10 (.in(n74ls161n_1_qa));
  _74LS161N u_74ls161n_1 (
    .VCC(1'b1), .QA(n74ls161n_1_qa), .QB(n74ls161n_1_qb), .QC(n74ls161n_1_qc), .QD(n74ls161n_1_qd),
    .T_En(1'b1), .LD(1'b1), .CLR(1'b0), .CLK(clock_1_out), .A(1'b0), .B(1'b0), .C(1'b0), .D(1'b0),
    .P_En(1'b1), .GND(1'b0));  // open: RCO
  Transistor #(.\type ("n"), .gate("br"), .width(8)) transistor_1 (
    .in(n28c16_1_dq0), .out(pull_resistor_9_node), .gate(n74ls04_1_y6));
  LED led_11 (.in(n74ls161n_1_qd));
  _28C16 u_28c16_1 (
    .VCC(1'b1), .DQ7(n28c16_1_dq0[7]), .DQ6(n28c16_1_dq0[6]), .DQ5(n28c16_1_dq0[5]), .DQ4(n28c16_1_dq0[4]),
    .DQ3(n28c16_1_dq0[3]), .A3(n74ls161n_1_qd), .A2(n74ls161n_1_qc), .A1(n74ls161n_1_qb),
    .A0(n74ls161n_1_qa), .DQ0(n28c16_1_dq0[0]), .DQ1(n28c16_1_dq0[1]), .DQ2(n28c16_1_dq0[2]), .GND(1'b0));  // open: W, DU, A8, A9, NC, G, A10, E, RB, NC_2, A7, A6, A5, A4
  _28C16 u_28c16_2 ();  // open: VCC, W, DU, A8, A9, NC, G, A10, E, DQ7, DQ6, DQ5, DQ4, DQ3, RB, NC_2, A7, A6, A5, A4, A3, A2, A1, A0, DQ0, DQ1, DQ2, GND

  // Notes on the sheet:
  //   161
  //   RI
  //   RO
  //   AO
endmodule

module _74LS86 (
  input  VCC,
  input  B4,
  input  A4,
  input  B3,
  input  A3,
  input  A1,
  input  B1,
  input  A2,
  input  B2,
  input  GND,
  output Y4,
  output Y3,
  output Y1,
  output Y2
);

  wire xor_1_out, xor_2_out, xor_3_out, xor_4_out;

  Transistor #(.\type ("n"), .gate("br")) transistor_1 (.in(xor_1_out), .out(Y4), .gate(VCC));
  xor xor_1 (xor_1_out, A4, B4);
  xor xor_2 (xor_2_out, A1, B1);
  Transistor #(.\type ("n"), .gate("br")) transistor_2 (.in(xor_2_out), .out(Y1), .gate(VCC));
  xor xor_3 (xor_3_out, A2, B2);
  Transistor #(.\type ("n"), .gate("br")) transistor_3 (.in(xor_4_out), .out(Y3), .gate(VCC));
  xor xor_4 (xor_4_out, A3, B3);
  Pull_Resistor pull_resistor_1 (.node(VCC));
  Transistor #(.\type ("n"), .gate("br")) transistor_4 (.in(xor_3_out), .out(Y2), .gate(VCC));

  // Notes on the sheet:
  //   XOR
endmodule

module _74LS08 (
  input  VCC,
  input  B4,
  input  A4,
  input  B3,
  input  A3,
  input  A1,
  input  B1,
  input  A2,
  input  B2,
  input  GND,
  output Y4,
  output Y3,
  output Y1,
  output Y2
);

  wire and_1_out, and_2_out, and_3_out, and_4_out;

  Transistor #(.\type ("n"), .gate("br")) transistor_1 (.in(and_1_out), .out(Y4), .gate(VCC));
  and and_1 (and_1_out, A4, B4);
  and and_2 (and_2_out, A1, B1);
  Transistor #(.\type ("n"), .gate("br")) transistor_2 (.in(and_2_out), .out(Y1), .gate(VCC));
  and and_3 (and_3_out, A2, B2);
  Transistor #(.\type ("n"), .gate("br")) transistor_3 (.in(and_4_out), .out(Y3), .gate(VCC));
  and and_4 (and_4_out, A3, B3);
  Pull_Resistor pull_resistor_1 (.node(VCC));
  Transistor #(.\type ("n"), .gate("br")) transistor_4 (.in(and_3_out), .out(Y2), .gate(VCC));

  // Notes on the sheet:
  //   AND
endmodule

module _74LS32 (
  input  VCC,
  input  B4,
  input  A4,
  input  B3,
  input  A3,
  input  A1,
  input  B1,
  input  A2,
  input  B2,
  input  GND,
  output Y4,
  output Y3,
  output Y1,
  output Y2
);

  wire or_1_out, or_2_out, or_3_out, or_4_out;

  Transistor #(.\type ("n"), .gate("br")) transistor_1 (.in(or_1_out), .out(Y4), .gate(VCC));
  or or_1 (or_1_out, A4, B4);
  or or_2 (or_2_out, A1, B1);
  Transistor #(.\type ("n"), .gate("br")) transistor_2 (.in(or_2_out), .out(Y1), .gate(VCC));
  or or_3 (or_3_out, A2, B2);
  Transistor #(.\type ("n"), .gate("br")) transistor_3 (.in(or_4_out), .out(Y3), .gate(VCC));
  or or_4 (or_4_out, A3, B3);
  Pull_Resistor pull_resistor_1 (.node(VCC));
  Transistor #(.\type ("n"), .gate("br")) transistor_4 (.in(or_3_out), .out(Y2), .gate(VCC));

  // Notes on the sheet:
  //   OR
endmodule

module _74LS04 (
  input  VCC,
  input  A6,
  input  A5,
  input  A4,
  input  A1,
  input  A2,
  input  A3,
  input  GND,
  output Y6,
  output Y5,
  output Y4,
  output Y1,
  output Y2,
  output Y3
);

  wire not_1_out, not_2_out, not_3_out, not_4_out, not_5_out, not_6_out;

  not not_1 (not_1_out, A1);
  Transistor #(.\type ("n"), .gate("br")) transistor_1 (.in(not_1_out), .out(Y1), .gate(VCC));
  Transistor #(.\type ("n"), .gate("br")) transistor_2 (.in(not_2_out), .out(Y6), .gate(VCC));
  not not_2 (not_2_out, A6);
  not not_3 (not_3_out, A2);
  Transistor #(.\type ("n"), .gate("br")) transistor_3 (.in(not_3_out), .out(Y2), .gate(VCC));
  Transistor #(.\type ("n"), .gate("br")) transistor_4 (.in(not_4_out), .out(Y5), .gate(VCC));
  not not_4 (not_4_out, A5);
  Transistor #(.\type ("n"), .gate("br")) transistor_5 (.in(not_5_out), .out(Y4), .gate(VCC));
  not not_5 (not_5_out, A4);
  Pull_Resistor pull_resistor_1 (.node(VCC));
  not not_6 (not_6_out, A3);
  Transistor #(.\type ("n"), .gate("br")) transistor_6 (.in(not_6_out), .out(Y3), .gate(VCC));

  // Notes on the sheet:
  //   NOT
endmodule

module _74LS161 (
  input  VCC,
  input  T_En,
  input  LD,
  input  CLK,
  input  A,
  input  B,
  input  C,
  input  D,
  input  P_En,
  input  GND,
  input  CLR,
  output RCO,
  output QA,
  output QB,
  output QC,
  output QD
);

  wire and_1_out, and_2_out, and_4_out, and_5_out, and_6_out, and_7_out, and_8_out, and_9_out, and_10_out,
       and_11_out, and_12_out, and_13_out, and_14_out, and_15_out, and_16_out, and_17_out, j_k_ff_1_qn,
       j_k_ff_2_qn, j_k_ff_3_qn, j_k_ff_4_qn, nand_1_out, nor_2_out, nor_3_out, nor_4_out, nor_5_out,
       nor_6_out, nor_7_out, nor_8_out, nor_9_out, nor_10_out, not_1_out, not_2_out, not_3_out;

  nor nor_1 (RCO, j_k_ff_4_qn, j_k_ff_3_qn, j_k_ff_2_qn, j_k_ff_1_qn);
  nor nor_2 (nor_2_out, and_2_out, and_1_out);
  and and_1 (and_1_out, nand_1_out, nor_3_out);
  and and_2 (and_2_out, QA, nor_5_out);
  not not_1 (not_1_out, CLK);
  // AND_Gate and_3 is placed but not wired
  J_K_Flip_Flop j_k_ff_1 (
    .J(nor_3_out), .clk(not_1_out), .K(nor_2_out), .Q(QA), .Qn(j_k_ff_1_qn), .en(VCC));  // open: preset, reset
  nor nor_3 (nor_3_out, and_4_out, and_5_out);
  and and_4 (and_4_out, A, CLR, nand_1_out);
  and and_5 (and_5_out, nor_5_out, j_k_ff_1_qn);
  nand nand_1 (nand_1_out, CLR, LD);
  nor nor_4 (nor_4_out, and_6_out, and_8_out);
  and and_6 (and_6_out, QB, QA, nor_5_out);
  nor nor_5 (nor_5_out, nand_1_out, not_3_out, not_2_out);
  J_K_Flip_Flop j_k_ff_2 (
    .J(nor_6_out), .clk(not_1_out), .K(nor_4_out), .Q(QB), .Qn(j_k_ff_2_qn), .en(VCC));  // open: preset, reset
  nor nor_6 (nor_6_out, and_7_out, and_9_out);
  and and_7 (and_7_out, B, CLR, nand_1_out);
  and and_8 (and_8_out, nand_1_out, nor_6_out);
  and and_9 (and_9_out, nor_5_out, QA, j_k_ff_2_qn);
  and and_10 (and_10_out, QC, QA, QB, nor_5_out);
  nor nor_7 (nor_7_out, and_10_out, and_12_out);
  and and_11 (and_11_out, C, CLR, nand_1_out);
  and and_12 (and_12_out, nand_1_out, nor_8_out);
  J_K_Flip_Flop j_k_ff_3 (
    .J(nor_8_out), .clk(not_1_out), .K(nor_7_out), .Q(QC), .Qn(j_k_ff_3_qn), .en(VCC));  // open: preset, reset
  nor nor_8 (nor_8_out, and_11_out, and_13_out);
  and and_13 (and_13_out, nor_5_out, QA, QB, j_k_ff_3_qn);
  nor nor_9 (nor_9_out, and_14_out, and_15_out);
  and and_14 (and_14_out, QD, QA, QB, QC, nor_5_out);
  and and_15 (and_15_out, nand_1_out, nor_10_out);
  J_K_Flip_Flop j_k_ff_4 (
    .J(nor_10_out), .clk(not_1_out), .K(nor_9_out), .Q(QD), .Qn(j_k_ff_4_qn), .en(VCC));  // open: preset, reset
  nor nor_10 (nor_10_out, and_17_out, and_16_out);
  and and_16 (and_16_out, nor_5_out, QA, QB, QC, j_k_ff_4_qn);
  and and_17 (and_17_out, D, CLR, nand_1_out);
  not not_2 (not_2_out, T_En);
  not not_3 (not_3_out, P_En);

  // Notes on the sheet:
  //   4Bit Counter
endmodule

module _74LS161N (
  input  VCC,
  input  T_En,
  input  LD,
  input  CLR,
  input  CLK,
  input  A,
  input  B,
  input  C,
  input  D,
  input  P_En,
  input  GND,
  output RCO,
  output QA,
  output QB,
  output QC,
  output QD
);

  wire and_1_out, and_2_out, and_3_out, and_4_out, and_5_out, and_6_out, and_7_out, and_8_out, and_9_out,
       and_10_out, and_11_out, and_13_out, buffer_1_out, nand_1_out, nand_2_out, nand_3_out, nand_4_out,
       nand_5_out, nand_6_out, nand_7_out, nand_8_out, nor_1_out, or_1_out, or_2_out, or_3_out, or_4_out;

  buf buffer_1 (buffer_1_out, CLR);
  and and_1 (and_1_out, nand_1_out, or_1_out);
  or or_1 (or_1_out, and_13_out, nor_1_out);
  nand nand_1 (nand_1_out, nor_1_out, nand_2_out);
  J_K_Flip_Flop j_k_ff_1 (.J(and_1_out), .clk(CLK), .K(and_2_out), .Q(QA), .en(VCC));  // open: Qn, preset, reset
  and and_2 (and_2_out, or_1_out, nand_2_out);
  nand nand_2 (nand_2_out, A, buffer_1_out, nor_1_out);
  nor nor_1 (nor_1_out, buffer_1_out, LD);
  J_K_Flip_Flop j_k_ff_2 (.J(and_4_out), .clk(CLK), .K(and_3_out), .Q(QB), .en(VCC));  // open: Qn, preset, reset
  and and_3 (and_3_out, or_2_out, nand_4_out);
  and and_4 (and_4_out, nand_3_out, or_2_out);
  or or_2 (or_2_out, and_5_out, nor_1_out);
  nand nand_3 (nand_3_out, nor_1_out, nand_4_out);
  nand nand_4 (nand_4_out, B, buffer_1_out, nor_1_out);
  and and_5 (and_5_out, QA, and_13_out);
  and and_6 (and_6_out, nand_5_out, or_3_out);
  nand nand_5 (nand_5_out, nor_1_out, nand_6_out);
  J_K_Flip_Flop j_k_ff_3 (.J(and_6_out), .clk(CLK), .K(and_7_out), .Q(QC), .en(VCC));  // open: Qn, preset, reset
  and and_7 (and_7_out, or_3_out, nand_6_out);
  or or_3 (or_3_out, and_8_out, nor_1_out);
  nand nand_6 (nand_6_out, C, buffer_1_out, nor_1_out);
  and and_8 (and_8_out, QA, QB, and_13_out);
  and and_9 (and_9_out, nand_7_out, or_4_out);
  or or_4 (or_4_out, and_10_out, nor_1_out);
  nand nand_7 (nand_7_out, nor_1_out, nand_8_out);
  and and_10 (and_10_out, QA, QB, QC, and_13_out);
  J_K_Flip_Flop j_k_ff_4 (.J(and_9_out), .clk(CLK), .K(and_11_out), .Q(QD), .en(VCC));  // open: Qn, preset, reset
  and and_11 (and_11_out, or_4_out, nand_8_out);
  nand nand_8 (nand_8_out, D, buffer_1_out, nor_1_out);
  and and_12 (RCO, QA, QB, QC, QD, T_En);
  and and_13 (and_13_out, P_En, T_En);

  // Notes on the sheet:
  //   4Bit Counter
endmodule

module _74LS173 (
  input  VCC,
  input  CLR,
  input  D1,
  input  D2,
  input  D3,
  input  D4,
  input  G2,
  input  G1,
  input  M,
  input  N,
  input  CLK,
  input  GND,
  output Q1,
  output Q2,
  output Q3,
  output Q4
);

  wire and_1_out, and_2_out, and_3_out, and_4_out, and_5_out, and_6_out, and_7_out, and_8_out, and_9_out,
       and_10_out, d_ff_1_q, d_ff_1_qn, d_ff_2_q, d_ff_2_qn, d_ff_3_q, d_ff_3_qn, d_ff_4_q, d_ff_4_qn,
       not_1_out, or_1_out, or_2_out, or_3_out, or_4_out;

  and and_1 (and_1_out, M, N);
  Pull_Resistor pull_resistor_1 (.node(M));
  Pull_Resistor pull_resistor_2 (.node(N));
  and and_2 (and_2_out, D1, and_10_out);
  and and_3 (and_3_out, d_ff_1_q, not_1_out);
  or or_1 (or_1_out, and_5_out, and_7_out);
  or or_2 (or_2_out, and_2_out, and_3_out);
  D_Flip_Flop d_ff_1 (.clk(CLK), .D(or_2_out), .Q(d_ff_1_q), .Qn(d_ff_1_qn), .en(VCC), .reset(CLR));  // open: preset
  assign Q2 = and_1_out ? ~d_ff_2_qn : 1'bz;  // Controlled_Inverter controlled_inverter_1
  assign Q1 = and_1_out ? ~d_ff_1_qn : 1'bz;  // Controlled_Inverter controlled_inverter_2
  and and_4 (and_4_out, D3, and_10_out);
  and and_5 (and_5_out, D2, and_10_out);
  and and_6 (and_6_out, d_ff_3_q, not_1_out);
  and and_7 (and_7_out, d_ff_2_q, not_1_out);
  or or_3 (or_3_out, and_4_out, and_6_out);
  D_Flip_Flop d_ff_2 (.clk(CLK), .D(or_1_out), .Q(d_ff_2_q), .Qn(d_ff_2_qn), .en(VCC), .reset(CLR));  // open: preset
  D_Flip_Flop d_ff_3 (.clk(CLK), .D(or_3_out), .Q(d_ff_3_q), .Qn(d_ff_3_qn), .en(VCC), .reset(CLR));  // open: preset
  assign Q3 = and_1_out ? ~d_ff_3_qn : 1'bz;  // Controlled_Inverter controlled_inverter_3
  and and_8 (and_8_out, D4, and_10_out);
  and and_9 (and_9_out, d_ff_4_q, not_1_out);
  or or_4 (or_4_out, and_8_out, and_9_out);
  D_Flip_Flop d_ff_4 (.clk(CLK), .D(or_4_out), .Q(d_ff_4_q), .Qn(d_ff_4_qn), .en(VCC), .reset(CLR));  // open: preset
  assign Q4 = and_1_out ? ~d_ff_4_qn : 1'bz;  // Controlled_Inverter controlled_inverter_4
  and and_10 (and_10_out, G2, G1);
  not not_1 (not_1_out, and_10_out);
  Pull_Resistor pull_resistor_3 (.node(CLR));
  Pull_Resistor pull_resistor_4 (.node(VCC));
  Pull_Resistor pull_resistor_5 (.node(CLK));

  // Notes on the sheet:
  //   4Bit Register
endmodule

module _74LS174 (
  input  VCC,
  input  D6,
  input  D5,
  input  D4,
  input  CLK,
  input  CLR,
  input  D1,
  input  D2,
  input  D3,
  input  GND,
  output Q6,
  output Q5,
  output Q4,
  output Q1,
  output Q2,
  output Q3
);

  wire pull_resistor_1_node;

  D_Flip_Flop d_ff_1 (.clk(CLK), .D(D6), .Q(Q6), .en(VCC), .reset(CLR));  // open: Qn, preset
  D_Flip_Flop d_ff_2 (.clk(CLK), .D(D1), .Q(Q1), .en(VCC), .reset(CLR));  // open: Qn, preset
  D_Flip_Flop d_ff_3 (.clk(CLK), .D(D5), .Q(Q5), .en(VCC), .reset(CLR));  // open: Qn, preset
  D_Flip_Flop d_ff_4 (.clk(CLK), .D(D2), .Q(Q2), .en(VCC), .reset(CLR));  // open: Qn, preset
  D_Flip_Flop d_ff_5 (.clk(CLK), .D(D4), .Q(Q4), .en(VCC), .reset(CLR));  // open: Qn, preset
  D_Flip_Flop d_ff_6 (.clk(CLK), .D(D3), .Q(Q3), .en(VCC), .reset(CLR));  // open: Qn, preset
  Pull_Resistor pull_resistor_1 (.node(pull_resistor_1_node));

  // Notes on the sheet:
  //   6 D FLIP FLOP
  //   D FLIP FLOP
endmodule

module _74LS245 (
  input  VCC,
  input  G,
  input  B1,
  input  B2,
  input  B3,
  input  B4,
  input  B5,
  input  B6,
  input  B7,
  input  B8,
  input  DIR,
  input  A1,
  input  A2,
  input  A3,
  input  A4,
  input  A5,
  input  A6,
  input  A7,
  input  A8,
  input  GND,
  output B1_2,
  output B2_2,
  output B3_2,
  output B4_2,
  output B5_2,
  output B6_2,
  output B7_2,
  output B8_2,
  output A1_2,
  output A2_2,
  output A3_2,
  output A4_2,
  output A5_2,
  output A6_2,
  output A7_2,
  output A8_2
);

  wire and_1_out, and_2_out, not_1_out;

  not not_1 (not_1_out, DIR);
  and and_1 (and_1_out, not_1_out, G);
  assign B1 = and_2_out ? A1 : 1'bz;  // Controlled_Buffer controlled_buffer_1
  and and_2 (and_2_out, DIR, G);
  assign A1 = and_1_out ? B1 : 1'bz;  // Controlled_Buffer controlled_buffer_2

  assign A1_2 = A1;
  assign B1_2 = B1;

  // Notes on the sheet:
  //   A1: pull=down
  //   A1_2: pull=down
endmodule

module _00LS245 (
  input  VCC,
  input  G,
  input  B1,
  input  B2,
  input  B3,
  input  B4,
  input  B5,
  input  B6,
  input  B7,
  input  B8,
  input  DIR,
  input  GND,
  output A1,
  output A2,
  output A3,
  output A4,
  output A5,
  output A6,
  output A7,
  output A8
);

  wire and_1_out, not_1_out;

  Pull_Resistor pull_resistor_1 (.node(G));
  and and_1 (and_1_out, not_1_out, G);
  not not_1 (not_1_out, DIR);
  Pull_Resistor pull_resistor_2 (.node(DIR));
  assign A1 = and_1_out ? B1 : 1'bz;  // Controlled_Buffer controlled_buffer_1
  assign A2 = and_1_out ? B2 : 1'bz;  // Controlled_Buffer controlled_buffer_2
  assign A3 = and_1_out ? B3 : 1'bz;  // Controlled_Buffer controlled_buffer_3
  assign A4 = and_1_out ? B4 : 1'bz;  // Controlled_Buffer controlled_buffer_4
  assign A5 = and_1_out ? B5 : 1'bz;  // Controlled_Buffer controlled_buffer_5
  assign A6 = and_1_out ? B6 : 1'bz;  // Controlled_Buffer controlled_buffer_6
  assign A8 = and_1_out ? B8 : 1'bz;  // Controlled_Buffer controlled_buffer_7
  assign A7 = and_1_out ? B7 : 1'bz;  // Controlled_Buffer controlled_buffer_8

  // Notes on the sheet:
  //   A1: pull=down
endmodule

module _74LS283 (
  input  VCC,
  input  B3,
  input  A3,
  input  A4,
  input  B4,
  input  B2,
  input  A2,
  input  A1,
  input  B1,
  input  C0,
  input  GND,
  output E3,
  output E4,
  output C4,
  output E2,
  output E1
);

  Pull_Resistor pull_resistor_1 (.node(B3));
  Pull_Resistor pull_resistor_2 (.node(VCC));
  Pull_Resistor pull_resistor_3 (.node(B2));
  Pull_Resistor pull_resistor_4 (.node(A3));
  Pull_Resistor pull_resistor_5 (.node(A2));
  Pull_Resistor pull_resistor_6 (.node(A4));
  Pull_Resistor pull_resistor_7 (.node(B4));
  Adder #(.width(4)) adder_1 (.a({A4, A3, A2, A1}), .b({B4, B3, B2, B1}), .out({E4, E3, E2, E1}), .cin(C0), .cout(C4));
  Pull_Resistor pull_resistor_8 (.node(A1));
  Pull_Resistor pull_resistor_9 (.node(B1));
  Pull_Resistor pull_resistor_10 (.node(C4));
  Pull_Resistor pull_resistor_11 (.node(C0));

  // Notes on the sheet:
  //   FULL ADDER
endmodule

module _28C16 (
  input  VCC,
  input  W,
  input  DU,
  input  A8,
  input  A9,
  input  NC,
  input  G,
  input  A10,
  input  E,
  input  RB,
  input  NC_2,
  input  A7,
  input  A6,
  input  A5,
  input  A4,
  input  A3,
  input  A2,
  input  A1,
  input  A0,
  input  GND,
  output DQ7,
  output DQ6,
  output DQ5,
  output DQ4,
  output DQ3,
  output DQ0,
  output DQ1,
  output DQ2
);

  Pull_Resistor pull_resistor_1 (.node(A8));
  Pull_Resistor pull_resistor_2 (.node(A7));
  Pull_Resistor pull_resistor_3 (.node(A9));
  Pull_Resistor pull_resistor_4 (.node(A5));
  Pull_Resistor pull_resistor_5 (.node(A6));
  Pull_Resistor pull_resistor_6 (.node(A4));
  Pull_Resistor pull_resistor_7 (.node(A10));
  Pull_Resistor pull_resistor_8 (.node(A3));
  Pull_Resistor pull_resistor_9 (.node(A2));
  RAM #(.addrWidth(11), .bus("asynch")) ram_1 (
    .addr({A10, A9, A8, A7, A6, A5, A4, A3, A2, A1, A0}), .data({DQ7, DQ6, DQ5, DQ4, DQ3, DQ2, DQ1, DQ0}),
    .sel(VCC), .ld(VCC));  // open: clr
  Pull_Resistor pull_resistor_10 (.node(A1));
  Pull_Resistor pull_resistor_11 (.node(A0));

  // Notes on the sheet:
  //   NC_2: pull=down
endmodule
