// Logisim project OR_SRFF.circ as structural Verilog: 1 circuit, main circuit main
module main (
  input  in_1,
  input  in_2,
  input  in_3,
  input  in_4,
  input  in_5,
  input  in_6,
  input  in_7,
  input  in_8,
  input  in_9,
  input  in_10,
  input  in_11,
  input  in_12,
  input  in_13,
  input  in_14
);

  wire clock_1_out, nor_1_out, nor_2_out, not_1_out, pull_resistor_1_node, pull_resistor_2_node, s_r_ff_1_q,
       transistor_1_out, transistor_2_out, transistor_3_out, transistor_4_out, transistor_7_out,
       transistor_10_out, transistor_13_out, transistor_15_out, transistor_17_out;

  Transistor #(.\type ("n")) transistor_1 (.in(1'b1), .out(transistor_1_out), .gate(in_2));
  Pull_Resistor pull_resistor_1 (.node(pull_resistor_1_node));
  Transistor #(.\type ("n")) transistor_2 (.in(1'b1), .out(transistor_2_out), .gate(in_5));
  Pull_Resistor pull_resistor_2 (.node(pull_resistor_2_node));
  Transistor #(.\type ("n")) transistor_3 (.in(1'b1), .out(transistor_3_out), .gate(transistor_13_out));
  Transistor transistor_4 (.in(1'b0), .out(transistor_4_out), .gate(in_2));
  Transistor transistor_5 (.in(transistor_4_out), .out(transistor_1_out), .gate(in_3));
  LED led_1 (.in(transistor_1_out));
  Transistor #(.\type ("n")) transistor_6 (.in(1'b1), .out(transistor_1_out), .gate(in_3));
  Transistor transistor_7 (.in(pull_resistor_1_node), .out(transistor_7_out), .gate(in_5));
  Transistor transistor_8 (.in(transistor_7_out), .out(transistor_2_out), .gate(transistor_15_out));
  Transistor #(.\type ("n")) transistor_9 (.in(1'b1), .out(transistor_2_out), .gate(transistor_15_out));
  Transistor transistor_10 (.in(pull_resistor_2_node), .out(transistor_10_out), .gate(transistor_13_out));
  Transistor transistor_11 (.in(transistor_10_out), .out(transistor_3_out), .gate(in_13));
  Transistor #(.\type ("n")) transistor_12 (.in(1'b1), .out(transistor_3_out), .gate(in_13));
  Transistor transistor_13 (.in(pull_resistor_1_node), .out(transistor_13_out), .gate(transistor_2_out));
  Transistor #(.\type ("n")) transistor_14 (.in(1'b1), .out(transistor_13_out), .gate(transistor_2_out));
  LED led_2 (.in(transistor_13_out));
  Transistor transistor_15 (.in(pull_resistor_2_node), .out(transistor_15_out), .gate(transistor_3_out));
  LED led_3 (.in(transistor_15_out));
  Transistor #(.\type ("n")) transistor_16 (.in(1'b1), .out(transistor_15_out), .gate(transistor_3_out));
  nor nor_1 (nor_1_out, in_1, nor_2_out);
  nor nor_2 (nor_2_out, nor_1_out, in_4);
  Clock clock_1 (.out(clock_1_out));
  Transistor #(.\type ("n")) transistor_17 (.in(in_8), .out(transistor_17_out), .gate(in_12));
  Pull_Resistor pull_resistor_3 (.node(transistor_17_out));
  not not_1 (not_1_out, transistor_17_out);
  Transistor #(.\type ("n"), .gate("br")) transistor_18 (.in(not_1_out), .out(in_8), .gate(in_14));
  LED led_4 (.in(nor_1_out));
  LED led_5 (.in(nor_2_out));
  S_R_Flip_Flop s_r_ff_1 (.S(in_6), .clk(clock_1_out), .R(in_7), .Q(s_r_ff_1_q), .en(1'b1));  // open: Qn, preset, reset
  // Probe on s_r_ff_1_q
  Register register_1 ();  // open: D, en, Q, clk, clr
  Multiplexer multiplexer_1 ();  // open: in0, in1, out, sel, en
endmodule
