// Logisim project RAM.circ as structural Verilog: 4 circuits, main circuit RAM
module RAM (
  input  a0,
  input  a1,
  input  a2,
  input  a3,
  input  a4,
  input  a5,
  input  a6,
  input  a7,
  input  d0,
  input  d1,
  input  d2,
  input  d3,
  input  d4,
  input  d5,
  input  d6,
  input  r_w,
  input  pow,
  input  clk,
  input  ld,
  input  clr,
  input  d7,
  output o0,
  output o1,
  output o2,
  output o3,
  output o4,
  output o5,
  output o6,
  output o7
);

  RAM_part #(.bus("separate")) ram_1 (
    .addr({a7, a6, a5, a4, a3, a2, a1, a0}), .din({d7, d6, d5, d4, d3, d2, d1, d0}),
    .data({o7, o6, o5, o4, o3, o2, o1, o0}), .str(r_w), .sel(pow), .clk(clk), .ld(ld), .clr(clr));

  // Notes on the sheet:
  //   reference / pointer / address
  //   write data
  //   read (0)
  //   write (1)
  //   go (1)
  //   clear
endmodule

module MAIN (
  input  [7:0] in_1,
  input  in_2,
  input  in_3,
  input  in_4,
  input  [7:0] dx,
  input  in_6,
  output [7:0] out_7
);

  wire clock_1_out;
  wire [1:0] counter_1_q_3;
  wire [2:0] counter_1_q, counter_1_q_2;
  wire [7:0] ram_1_o0, rom_1_o0, switch_1_out_10, switch_1_out_11, switch_1_out_12, switch_1_out_13,
       switch_1_out_14, switch_1_out_15, switch_1_out_16, switch_1_out_17;

  Clock clock_1 (.out(clock_1_out));
  Counter counter_1 (
    .load(in_2), .D({counter_1_q_3, counter_1_q_2, counter_1_q}), .count(in_3),
    .Q({counter_1_q_3, counter_1_q_2, counter_1_q}), .clk(clock_1_out), .clr(in_4));  // open: carry
  ROM rom_1 (
    .a0(counter_1_q[0]), .a1(counter_1_q[1]), .a2(counter_1_q[2]), .a3(counter_1_q_2[0]),
    .a4(counter_1_q_2[1]), .a5(counter_1_q_2[2]), .a6(counter_1_q_3[0]), .a7(counter_1_q_3[1]),
    .o0(rom_1_o0[0]), .o1(rom_1_o0[1]), .o2(rom_1_o0[2]), .o3(rom_1_o0[3]), .o4(rom_1_o0[4]),
    .o5(rom_1_o0[5]), .o6(rom_1_o0[6]), .o7(rom_1_o0[7]), .pow(in_6));
  Shifter #(.shift("rl")) shifter_1 (.in(in_1), .\dist (counter_1_q), .out(out_7));
  RAM ram_1 (
    .a0(counter_1_q[0]), .a1(counter_1_q[1]), .a2(counter_1_q[2]), .a3(counter_1_q_2[0]),
    .a4(counter_1_q_2[1]), .a5(counter_1_q_2[2]), .a6(counter_1_q_3[0]), .a7(counter_1_q_3[1]),
    .o0(ram_1_o0[0]), .o1(ram_1_o0[1]), .o2(ram_1_o0[2]), .o3(ram_1_o0[3]), .o4(ram_1_o0[4]),
    .o5(ram_1_o0[5]), .o6(ram_1_o0[6]), .o7(ram_1_o0[7]), .pow(dx[1]), .ld(dx[2]), .clr(dx[3]), .r_w(dx[0]),
    .d0(rom_1_o0[0]), .d1(rom_1_o0[1]), .d2(rom_1_o0[2]), .d3(rom_1_o0[3]), .d4(rom_1_o0[4]),
    .d5(rom_1_o0[5]), .d6(rom_1_o0[6]), .d7(rom_1_o0[7]), .clk(clock_1_out));
  LED led_1 (.in(clock_1_out));
  DotMatrix #(.inputtype("row"), .matrixcols(8), .matrixrows(8), .persist(8)) dotmatrix_1 (
    .row0(switch_1_out_10), .row1(switch_1_out_11), .row2(switch_1_out_12), .row3(switch_1_out_13),
    .row4(switch_1_out_14), .row5(switch_1_out_15), .row6(switch_1_out_16), .row7(switch_1_out_17));
  SWITCH switch_1 (
    .in_2(ram_1_o0), .in_3(ram_1_o0), .in_4(ram_1_o0), .in_5(ram_1_o0), .in_6(ram_1_o0), .in_7(ram_1_o0),
    .in_8(ram_1_o0), .in_9(ram_1_o0), .out_10(switch_1_out_10), .out_11(switch_1_out_11),
    .out_12(switch_1_out_12), .out_13(switch_1_out_13), .out_14(switch_1_out_14), .out_15(switch_1_out_15),
    .out_16(switch_1_out_16), .out_17(switch_1_out_17), .in_1(out_7));
endmodule

module SWITCH (
  input  [7:0] in_1,
  input  [7:0] in_2,
  input  [7:0] in_3,
  input  [7:0] in_4,
  input  [7:0] in_5,
  input  [7:0] in_6,
  input  [7:0] in_7,
  input  [7:0] in_8,
  input  [7:0] in_9,
  output [7:0] out_10,
  output [7:0] out_11,
  output [7:0] out_12,
  output [7:0] out_13,
  output [7:0] out_14,
  output [7:0] out_15,
  output [7:0] out_16,
  output [7:0] out_17
);

  Transistor #(.\type ("n"), .width(8)) transistor_1 (.in(in_2), .out(out_10), .gate(in_1[0]));
  Transistor #(.\type ("n"), .width(8)) transistor_2 (.in(in_3), .out(out_11), .gate(in_1[1]));
  Transistor #(.\type ("n"), .width(8)) transistor_3 (.in(in_4), .out(out_12), .gate(in_1[2]));
  Transistor #(.\type ("n"), .width(8)) transistor_4 (.in(in_5), .out(out_13), .gate(in_1[3]));
  Transistor #(.\type ("n"), .width(8)) transistor_5 (.in(in_6), .out(out_14), .gate(in_1[4]));
  Pull_Resistor pull_resistor_1 (.node(out_10));
  Transistor #(.\type ("n"), .width(8)) transistor_6 (.in(in_7), .out(out_15), .gate(in_1[5]));
  Transistor #(.\type ("n"), .width(8)) transistor_7 (.in(in_8), .out(out_16), .gate(in_1[6]));
  Transistor #(.\type ("n"), .width(8)) transistor_8 (.in(in_9), .out(out_17), .gate(in_1[7]));
  Pull_Resistor pull_resistor_2 (.node(out_11));
  Pull_Resistor pull_resistor_3 (.node(out_13));
  Pull_Resistor pull_resistor_4 (.node(out_14));
  Pull_Resistor pull_resistor_5 (.node(out_12));
  Pull_Resistor pull_resistor_6 (.node(out_16));
  Pull_Resistor pull_resistor_7 (.node(out_17));
  Pull_Resistor pull_resistor_8 (.node(out_15));
endmodule

module ROM (
  input  a0,
  input  a1,
  input  a2,
  input  a3,
  input  a4,
  input  a5,
  input  a6,
  input  a7,
  input  pow,
  output o0,
  output o1,
  output o2,
  output o3,
  output o4,
  output o5,
  output o6,
  output o7
);

  ROM_part rom_1 (.addr({a7, a6, a5, a4, a3, a2, a1, a0}), .data({o7, o6, o5, o4, o3, o2, o1, o0}), .sel(pow));

  // Notes on the sheet:
  //   reference / pointer / address
  //   contents of rom_1 (hex, n*v repeats v):
  //   aa d ad 0 fd 0 f 0 f af d f df 0 df 0 af d f df 0 df 0 df d f df 0 df a df af 0 df d f d df d f af
  //   ff da fa d f f 0 0 f d 0 f d 0 af df a f da f ad f df df f ad f df ff df af da fd fa f df af fa f da
  //   ff af aa df a df da fa df df a df ad df
endmodule
